# Fritzing sketch wiring (saved by Fritzing 1.0.0d)
perfboards: 1

parts:
  RGB_SMD_LED1 = SMD RGB LED (WS2812) [package=5050]
  S1 = Round Pushbutton
  J1 = female pin header, 4 pins [form="♀ (female)"]
  J2 = female pin header, 6 pins [form="♀ (female)"]
  R2 = Resistor [tolerance=±5% resistance=10k package="0603 [SMD]"]

nets:
  N1: RGB_SMD_LED1.DIn, J1.pin3
  N2: RGB_SMD_LED1.VCC, J1.pin2
  N3: RGB_SMD_LED1.NC, J2.pin2, R2.Pin_0
  N4: S1.leg0, J2.pin3
  N5: S1.leg1, J1.pin1, R2.Pin_1
